// Logisim project sagui.circ as structural Verilog: 4 circuits, main circuit main
module main (
  output [7:0] out_1,
  output [7:0] out_2,
  output [3:0] out_3,
  output [7:0] out_4,
  output [7:0] out_5,
  output [3:0] out_6,
  output [7:0] out_7,
  output [7:0] out_8,
  output [7:0] out_9,
  output [7:0] out_10,
  output [7:0] out_11,
  output [7:0] out_12
);

  wire and_1_out, and_2_out, Clk, I_type, isZero, jumpPC, memToReg, memWrite, not_1_out, regWrite;
  wire [1:0] multiplexer_3_out;
  wire [3:0] ctrl, rom_1_data;
  wire [7:0] adder_1_out, multiplexer_1_out, multiplexer_2_out, multiplexer_4_out, PC_q, ram_1_dout;
  wire [9:8] memoriaDeControle_data;

  Multiplexer #(.width(8)) multiplexer_1 (.in0(8'h1), .in1(multiplexer_4_out), .out(multiplexer_1_out), .sel(jumpPC));
  Adder adder_1 (.a(PC_q), .b(multiplexer_1_out), .out(adder_1_out), .cin(1'b0));  // open: cout
  and and_1 (and_1_out, jumpPC, ~I_type);  // AND_Gate
  ROM #(.addrWidth(4), .dataWidth(10)) memoriaDeControle (
    .addr(ctrl), .data({memoriaDeControle_data, memToReg, memWrite, regWrite, I_type, out_3}));
  Multiplexer #(.width(8)) multiplexer_2 (
    .in0(adder_1_out), .in1(multiplexer_4_out), .out(multiplexer_2_out), .sel(and_1_out));
  Register PC (.D(multiplexer_2_out), .en(1'b1), .clk(Clk), .Q(PC_q), .clr(1'b0));
  ROM rom_1 (.addr(PC_q), .data({ctrl, rom_1_data}));
  or or_1 (jumpPC, memoriaDeControle_data[8], and_2_out);
  and and_2 (and_2_out, memoriaDeControle_data[9], isZero);
  Clock clock_Global (.out(Clk));
  assign out_8 = {{4{rom_1_data[3]}}, rom_1_data};  // Bit_Extender bit_extender_1
  Multiplexer #(.width(2)) multiplexer_3 (.in0(rom_1_data[3:2]), .in1(2'b00), .out(multiplexer_3_out), .sel(I_type));
  BancoRegistradores bancoregistradores_1 (
    .WE(regWrite), .write_data(out_9), .clk(Clk), .a_adress(multiplexer_3_out), .b_adress(rom_1_data[1:0]),
    .a_data(out_1), .b_data(out_7));
  Multiplexer #(.width(8)) multiplexer_4 (.in0(out_7), .in1(out_8), .out(multiplexer_4_out), .sel(I_type));
  ULA ula_1 (.a(out_1), .b(multiplexer_4_out), .selector(out_3), .result(out_2), .isZero(isZero));
  not not_1 (not_1_out, memWrite);
  RAM #(.asyncread("true")) ram_1 (
    .addr(out_2), .we(memWrite), .oe(not_1_out), .clk(Clk), .din(out_1), .dout(ram_1_dout));
  Multiplexer #(.width(8)) multiplexer_5 (.in0(out_2), .in1(ram_1_dout), .out(out_9), .sel(memToReg));

  assign out_4 = out_1;
  assign out_5 = out_2;
  assign out_6 = out_3;
  assign out_10 = out_7;
  assign out_11 = out_8;
  assign out_12 = out_9;

  // Other names for the same wires on the sheet: selectorALU[3:0] = out_3; aData[7:0] = out_1; aluResult[7:0] = out_2;
  //   bData[7:0] = out_7; immediate[7:0] = out_8; writingData[7:0] = out_9

  // Notes on the sheet:
  //   Somador
  //   contents of memoriaDeControle (hex, n*v repeats v):
  //   209 219 100 110 a9 49 29 37 38 20 21 22 23 24 25 26
  //   Memoria de Controle
  //   contents of rom_1 (hex, n*v repeats v):
  //   82 64 7 71 68 a2 1f dc df fd e9 99 5d be 4d 4d c6 46 6 40*0 30 14*0 23
  //   branch
  //   Memoria de Instrucoes
  //   Memoria de Dados
endmodule

module ULA (
  input  [7:0] a,
  input  [7:0] b,
  input  [3:0] selector,
  output [7:0] result,
  output isZero
);

  wire or_2_out;
  wire [7:0] adder_1_out, and_1_out, multiplexer_1_out, multiplexer_2_out, not_1_out, or_1_out,
       shifter_1_out, shifter_2_out, subtractor_1_out;
  wire [7:4] moveHigh;

  Bit_Extender #(.out_width(4)) bit_extender_1 (.in(b), .out(moveHigh));
  Adder adder_1 (.a(a), .b(b), .out(adder_1_out), .cin(1'b0));  // open: cout
  Subtractor subtractor_1 (.a(a), .b(b), .out(subtractor_1_out), .bin(1'b0));  // open: bout
  assign and_1_out = a & b;  // AND_Gate and_1, 8 bits wide
  assign or_1_out = a | b;  // OR_Gate or_1, 8 bits wide
  assign not_1_out = ~b;  // NOT_Gate not_1, 8 bits wide
  Shifter shifter_1 (.in(a), .\dist (b[2:0]), .out(shifter_1_out));
  Shifter #(.shift("lr")) shifter_2 (.in(a), .\dist (b[2:0]), .out(shifter_2_out));
  Multiplexer #(.width(8)) multiplexer_1 (
    .in0(shifter_1_out), .in1({8{1'b0}}), .out(multiplexer_1_out), .sel(or_2_out));
  Multiplexer #(.width(8)) multiplexer_2 (
    .in0(shifter_2_out), .in1({8{1'b0}}), .out(multiplexer_2_out), .sel(or_2_out));
  or or_2 (or_2_out, b[7], b[6], b[5], b[4], b[3]);
  Multiplexer #(.select(4), .width(8)) multiplexer_3 (
    .in0(adder_1_out), .in1(subtractor_1_out), .in2(and_1_out), .in3(or_1_out), .in4(not_1_out),
    .in5(multiplexer_1_out), .in6(multiplexer_2_out), .in7({moveHigh, a[3:0]}), .in8({a[7:4], moveHigh}),
    .in9(b), .in10({8{1'b0}}), .in11({8{1'b0}}), .in12({8{1'b0}}), .in13({8{1'b0}}), .in14({8{1'b0}}),
    .in15({8{1'b0}}), .out(result), .sel(selector));
  nor nor_1 (isZero, a[0], a[1], a[2], a[3], a[5], a[6], a[7], a[4]);

  // Other names for the same wires on the sheet: moveHigh[3:0] = a[3:0]; moveLow[7:0] = {a[7:4], moveHigh}

  // Notes on the sheet:
  //   Somador
  //   Subtrator
  //   And
  //   Or
  //   Not
  //   Logical Shifter Left
  //   Logical Shifter Right
  //   Move High
  //   Move Low
endmodule

module BancoRegistradores (
  input  WE,
  input  [7:0] write_data,
  input  clk,
  input  [1:0] a_adress,
  input  [1:0] b_adress,
  output [7:0] a_data,
  output [7:0] b_data
);

  wire demultiplexer_1_out0, demultiplexer_1_out1, demultiplexer_1_out2, demultiplexer_1_out3;
  wire [7:0] r_0_outpt, r_1_outpt, r_2_outpt, r_3_outpt;

  Demultiplexer #(.select(2)) demultiplexer_1 (
    .out0(demultiplexer_1_out0), .out1(demultiplexer_1_out1), .out2(demultiplexer_1_out2),
    .out3(demultiplexer_1_out3), .in(WE), .sel(a_adress));
  Registrador_8bit r_0 (.inpt(write_data), .WE(demultiplexer_1_out0), .clk(clk), .outpt(r_0_outpt));
  Registrador_8bit r_1 (.inpt(write_data), .WE(demultiplexer_1_out1), .clk(clk), .outpt(r_1_outpt));
  Registrador_8bit r_2 (.inpt(write_data), .WE(demultiplexer_1_out2), .clk(clk), .outpt(r_2_outpt));
  Registrador_8bit r_3 (.inpt(write_data), .WE(demultiplexer_1_out3), .clk(clk), .outpt(r_3_outpt));
  Multiplexer #(.select(2), .width(8)) multiplexer_1 (
    .in0(r_0_outpt), .in1(r_1_outpt), .in2(r_2_outpt), .in3(r_3_outpt), .out(a_data), .sel(a_adress));
  Multiplexer #(.select(2), .width(8)) multiplexer_2 (
    .in0(r_0_outpt), .in1(r_1_outpt), .in2(r_2_outpt), .in3(r_3_outpt), .out(b_data), .sel(b_adress));
endmodule

module Registrador_8bit (
  input  [7:0] inpt,
  input  WE,
  input  clk,
  output [7:0] outpt
);

  wire multiplexer_1_out, multiplexer_2_out, multiplexer_3_out, multiplexer_4_out, multiplexer_5_out,
       multiplexer_6_out, multiplexer_7_out, multiplexer_8_out;

  D_Flip_Flop d_ff_1 (.D(multiplexer_1_out), .clk(clk), .Q(outpt[3]));  // open: Qn, preset, reset
  Multiplexer multiplexer_1 (.in0(outpt[3]), .in1(inpt[3]), .out(multiplexer_1_out), .sel(WE));
  D_Flip_Flop d_ff_2 (.D(multiplexer_2_out), .clk(clk), .Q(outpt[7]));  // open: Qn, preset, reset
  Multiplexer multiplexer_2 (.in0(outpt[7]), .in1(inpt[7]), .out(multiplexer_2_out), .sel(WE));
  D_Flip_Flop d_ff_3 (.D(multiplexer_3_out), .clk(clk), .Q(outpt[2]));  // open: Qn, preset, reset
  Multiplexer multiplexer_3 (.in0(outpt[2]), .in1(inpt[2]), .out(multiplexer_3_out), .sel(WE));
  D_Flip_Flop d_ff_4 (.D(multiplexer_4_out), .clk(clk), .Q(outpt[6]));  // open: Qn, preset, reset
  Multiplexer multiplexer_4 (.in0(outpt[6]), .in1(inpt[6]), .out(multiplexer_4_out), .sel(WE));
  D_Flip_Flop d_ff_5 (.D(multiplexer_5_out), .clk(clk), .Q(outpt[1]));  // open: Qn, preset, reset
  Multiplexer multiplexer_5 (.in0(outpt[1]), .in1(inpt[1]), .out(multiplexer_5_out), .sel(WE));
  D_Flip_Flop d_ff_6 (.D(multiplexer_6_out), .clk(clk), .Q(outpt[5]));  // open: Qn, preset, reset
  Multiplexer multiplexer_6 (.in0(outpt[5]), .in1(inpt[5]), .out(multiplexer_6_out), .sel(WE));
  Multiplexer multiplexer_7 (.in0(outpt[0]), .in1(inpt[0]), .out(multiplexer_7_out), .sel(WE));
  Multiplexer multiplexer_8 (.in0(outpt[4]), .in1(inpt[4]), .out(multiplexer_8_out), .sel(WE));
  D_Flip_Flop d_ff_7 (.D(multiplexer_7_out), .clk(clk), .Q(outpt[0]));  // open: Qn, preset, reset
  D_Flip_Flop d_ff_8 (.D(multiplexer_8_out), .clk(clk), .Q(outpt[4]));  // open: Qn, preset, reset

  // Other names for the same wires on the sheet: t_0 = inpt[0]; t_1 = inpt[1]; t_2 = inpt[2]; t_3 = inpt[3];
  //   t_4 = inpt[4]; t_5 = inpt[5]; t_6 = inpt[6]; t_7 = inpt[7]; s_0 = outpt[0]; s_1 = outpt[1]; s_2 = outpt[2];
  //   s_3 = outpt[3]; s_4 = outpt[4]; s_5 = outpt[5]; s_6 = outpt[6]; s_7 = outpt[7]
endmodule
