// Logisim project saguiLongo.circ as structural Verilog: 8 circuits, main circuit main
module main (
  output [7:0] out_1,
  output [7:0] out_2,
  output [7:0] out_3,
  output [7:0] out_4,
  output [7:0] out_5,
  output [7:0] out_6,
  output [7:0] out_7,
  output [7:0] out_8
);

  wire and_1_out, Clk, ctrl_type_fu_1_iszero, mem_to_reg, mem_Write, not_1_out, not_2_out, or_1_out;
  wire [1:0] control_unit_1_pc_handler;
  wire [2:0] arith1_FU_selector, arith2_FU_selector, ctrl_FU_selector, data_FU_selector;
  wire [5:0] control_unit_1_arithm1, control_unit_1_arithm2, control_unit_1_ctrl, control_unit_1_data;
  wire [7:0] adder_1_out, arithmetic_type_fu_1_result, arithmetic_type_fu_2_result, ctrl_type_fu_1_pc_out,
       data_type_fu_1_result, multiplexer_1_out, multiplexer_2_out, PC_q, ram_1_dout, rom_1_p2, rom_1_p3,
       rom_1_p4, rom_1_p5;
  wire [15:0] register_file_1_arithm1_output, register_file_1_arithm2_output, register_file_1_ctrl_output,
       register_file_1_data_output;

  Adder adder_1 (.a(PC_q), .b(8'h4), .out(adder_1_out), .cin(1'b0));  // open: cout
  Multiplexer #(.width(8)) multiplexer_1 (
    .in0(adder_1_out), .in1(ctrl_type_fu_1_pc_out), .out(multiplexer_1_out), .sel(or_1_out));
  or or_1 (or_1_out, and_1_out, control_unit_1_pc_handler[1]);
  and and_1 (and_1_out, ctrl_type_fu_1_iszero, control_unit_1_pc_handler[0]);
  Register PC (.D(multiplexer_1_out), .en(1'b1), .clk(Clk), .Q(PC_q), .clr(1'b0));
  // ROM #(.line("quad"), .misaligned("true")) rom_1: pin names not known; wires that end beside it: PC_q, rom_1_p2, rom_1_p3, rom_1_p4, rom_1_p5
  Clock clock_Global (.out(Clk));
  Control_unit control_unit_1 (
    .i_00(rom_1_p2), .i_01(rom_1_p3), .i_02(rom_1_p4), .i_03(rom_1_p5), .data(control_unit_1_data),
    .arithm1(control_unit_1_arithm1), .arithm2(control_unit_1_arithm2), .ctrl(control_unit_1_ctrl),
    .data_FU_selector(data_FU_selector), .arith1_FU_selector(arith1_FU_selector),
    .arith2_FU_selector(arith2_FU_selector), .ctrl_FU_selector(ctrl_FU_selector), .mem_to_reg(mem_to_reg),
    .mem_write(mem_Write), .PC_handler(control_unit_1_pc_handler));
  Register_file register_file_1 (
    .clk(Clk), .WD_data(multiplexer_2_out), .WD_arith1(arithmetic_type_fu_1_result),
    .WD_arith2(arithmetic_type_fu_2_result), .data(control_unit_1_data), .arithm1(control_unit_1_arithm1),
    .arithm2(control_unit_1_arithm2), .ctrl(control_unit_1_ctrl), .data_output(register_file_1_data_output),
    .arithm1_output(register_file_1_arithm1_output), .arithm2_output(register_file_1_arithm2_output),
    .ctrl_output(register_file_1_ctrl_output), .reg_00(out_1), .reg_01(out_5), .reg_02(out_2), .reg_03(out_6));
  Data_type_FU data_type_fu_1 (
    .in_1(register_file_1_data_output), .selector(data_FU_selector), .result(data_type_fu_1_result));
  Arithmetic_type_FU arithmetic_type_fu_1 (
    .in_1(register_file_1_arithm1_output), .selector(arith1_FU_selector), .result(arithmetic_type_fu_1_result));
  Arithmetic_type_FU arithmetic_type_fu_2 (
    .in_1(register_file_1_arithm2_output), .selector(arith2_FU_selector), .result(arithmetic_type_fu_2_result));
  Ctrl_type_FU ctrl_type_fu_1 (
    .in_1(register_file_1_ctrl_output), .PC_in(PC_q), .selector(ctrl_FU_selector),
    .PC_out(ctrl_type_fu_1_pc_out), .isZero(ctrl_type_fu_1_iszero));
  not not_1 (not_1_out, mem_Write);
  RAM #(.asyncread("true")) ram_1 (
    .addr(register_file_1_data_output[7:0]), .we(mem_Write), .oe(not_1_out), .clk(Clk),
    .din(data_type_fu_1_result), .dout(ram_1_dout));
  not not_2 (not_2_out, mem_to_reg);
  Multiplexer #(.width(8)) multiplexer_2 (
    .in0(ram_1_dout), .in1(data_type_fu_1_result), .out(multiplexer_2_out), .sel(not_2_out));

  assign out_3 = out_1;
  assign out_4 = out_2;
  assign out_7 = out_5;
  assign out_8 = out_6;

  // Other names for the same wires on the sheet: r00[7:0] = out_1; r01[7:0] = out_5; r02[7:0] = out_2;
  //   r03[7:0] = out_6

  // Notes on the sheet:
  //   contents of rom_1 (hex, n*v repeats v):
  //   74 ff ff c8 6c 84 ad ff 9a e1 59 9 b8 4d d5 d 16 74 4*ff 32 ff 84 ff ff 13 70 21 ff ff
  //   Memoria de Instrucoes
  //   Ld/St address
  //   Memoria de Dados
endmodule

module Data_type_FU (
  input  [15:0] in_1,
  input  [2:0] selector,
  output [7:0] result
);

  wire [3:0] bit_extender_1_out;

  Bit_Extender #(.out_width(4)) bit_extender_1 (.in(in_1[7:0]), .out(bit_extender_1_out));
  Multiplexer #(.select(2), .width(8)) multiplexer_1 (
    .in0({bit_extender_1_out, in_1[11:8]}), .in1({in_1[15:12], bit_extender_1_out}), .in2(in_1[15:8]),
    .in3({8{1'b0}}), .out(result), .sel(selector[1:0]));

  // Other names for the same wires on the sheet: a[7:0] = in_1[15:8]; selector_t[1:0] = selector[1:0]

  // Notes on the sheet:
  //   Move High
  //   Move Low
  //   Ld/St data
endmodule

module Arithmetic_type_FU (
  input  [15:0] in_1,
  input  [2:0] selector,
  output [7:0] result
);

  wire or_2_out;
  wire [7:0] adder_1_out, and_1_out, multiplexer_1_out, multiplexer_2_out, not_1_out, or_1_out,
       shifter_1_out, shifter_2_out, subtractor_1_out;

  Adder adder_1 (.a(in_1[15:8]), .b(in_1[7:0]), .out(adder_1_out), .cin(1'b0));  // open: cout
  Subtractor subtractor_1 (.a(in_1[15:8]), .b(in_1[7:0]), .out(subtractor_1_out), .bin(1'b0));  // open: bout
  assign and_1_out = in_1[15:8] & in_1[7:0];  // AND_Gate and_1, 8 bits wide
  assign or_1_out = in_1[15:8] | in_1[7:0];  // OR_Gate or_1, 8 bits wide
  assign not_1_out = ~in_1[7:0];  // NOT_Gate not_1, 8 bits wide
  Shifter shifter_1 (.in(in_1[15:8]), .\dist (in_1[2:0]), .out(shifter_1_out));
  Shifter #(.shift("lr")) shifter_2 (.in(in_1[15:8]), .\dist (in_1[2:0]), .out(shifter_2_out));
  Multiplexer #(.width(8)) multiplexer_1 (
    .in0(shifter_1_out), .in1({8{1'b0}}), .out(multiplexer_1_out), .sel(or_2_out));
  Multiplexer #(.width(8)) multiplexer_2 (
    .in0(shifter_2_out), .in1({8{1'b0}}), .out(multiplexer_2_out), .sel(or_2_out));
  or or_2 (or_2_out, in_1[7], in_1[6], in_1[5], in_1[4], in_1[3]);
  Multiplexer #(.select(3), .width(8)) multiplexer_3 (
    .in0(adder_1_out), .in1(subtractor_1_out), .in2(and_1_out), .in3(or_1_out), .in4(not_1_out),
    .in5(multiplexer_1_out), .in6(multiplexer_2_out), .in7({8{1'b0}}), .out(result), .sel(selector));

  // Other names for the same wires on the sheet: a[7:0] = in_1[15:8]

  // Notes on the sheet:
  //   Somador
  //   Subtrator
  //   And
  //   Or
  //   Not
  //   Logical Shifter Left
  //   Logical Shifter Right
endmodule

module Ctrl_type_FU (
  input  [15:0] in_1,
  input  [7:0] PC_in,
  input  [2:0] selector,
  output [7:0] PC_out,
  output isZero
);

  wire [7:0] adder_1_out, multiplexer_1_out, multiplexer_2_out;

  nor nor_1 (isZero, in_1[8], in_1[9], in_1[10], in_1[11], in_1[13], in_1[14], in_1[15], in_1[12]);
  Adder adder_1 (.a(in_1[7:0]), .b(PC_in), .out(adder_1_out), .cin(1'b0));  // open: cout
  Multiplexer #(.width(8)) multiplexer_1 (.in0(PC_in), .in1(in_1[7:0]), .out(multiplexer_1_out), .sel(isZero));
  Multiplexer #(.width(8)) multiplexer_2 (.in0(PC_in), .in1(adder_1_out), .out(multiplexer_2_out), .sel(isZero));
  Multiplexer #(.select(3), .width(8)) multiplexer_3 (
    .in0(in_1[7:0]), .in1(adder_1_out), .in2(multiplexer_1_out), .in3(multiplexer_2_out), .in4(PC_in),
    .in5(PC_in), .in6(PC_in), .in7(PC_in), .out(PC_out), .sel(selector));

  // Other names for the same wires on the sheet: a[7:0] = in_1[15:8]

  // Notes on the sheet:
  //   PC + Imm
  //   Jump Register
  //   Jump Immediate
  //   Branch On Zero Register
  //   Branch On Zero Immediate
endmodule

module Register_file (
  input  clk,
  input  [7:0] WD_data,
  input  [7:0] WD_arith1,
  input  [7:0] WD_arith2,
  input  [5:0] data,
  input  [5:0] arithm1,
  input  [5:0] arithm2,
  input  [5:0] ctrl,
  output [15:0] data_output,
  output [15:0] arithm1_output,
  output [15:0] arithm2_output,
  output [15:0] ctrl_output,
  output [7:0] reg_00,
  output [7:0] reg_01,
  output [7:0] reg_02,
  output [7:0] reg_03
);

  wire xor_1_out, xor_2_out, xor_3_out, xor_4_out;
  wire [1:0] ctrl_a_address, data_a_address;
  wire [2:0] decoder_1_out0, decoder_1_out1, decoder_1_out2, decoder_1_out3;
  wire [7:0] ctrl_immediate, data_immediate, multiplexer_3_out, multiplexer_4_out, multiplexer_5_out,
       multiplexer_6_out, multiplexer_8_out, multiplexer_14_out;

  // NoConnect on arithm1[5]
  // NoConnect on arithm2[5]
  Decoder #(.select(2)) decoder_1 (
    .out0(decoder_1_out0[0]), .out1(decoder_1_out1[0]), .out2(decoder_1_out2[0]), .out3(decoder_1_out3[0]),
    .sel(data_a_address), .en(data[4]));
  Decoder #(.select(2)) decoder_2 (
    .out0(decoder_1_out0[1]), .out1(decoder_1_out1[1]), .out2(decoder_1_out2[1]), .out3(decoder_1_out3[1]),
    .sel(arithm1[3:2]), .en(arithm1[4]));
  Decoder #(.select(2)) decoder_3 (
    .out0(decoder_1_out0[2]), .out1(decoder_1_out1[2]), .out2(decoder_1_out2[2]), .out3(decoder_1_out3[2]),
    .sel(arithm2[3:2]), .en(arithm2[4]));
  assign data_immediate = {{4{data[3]}}, data[3:0]};  // Bit_Extender bit_extender_1
  Multiplexer #(.width(2)) multiplexer_1 (.in0(ctrl[3:2]), .in1(2'b00), .out(ctrl_a_address), .sel(ctrl[5]));
  assign ctrl_immediate = {{4{ctrl[3]}}, ctrl[3:0]};  // Bit_Extender bit_extender_2
  Multiplexer #(.width(2)) multiplexer_2 (.in0(data[3:2]), .in1(2'b00), .out(data_a_address), .sel(data[5]));
  Multiplexer #(.select(3), .width(8)) multiplexer_3 (
    .in0({8{1'b0}}), .in1(WD_data), .in2(WD_arith1), .in3({8{1'b0}}), .in4(WD_arith2), .in5({8{1'b0}}),
    .in6({8{1'b0}}), .in7({8{1'b0}}), .out(multiplexer_3_out), .sel(decoder_1_out0));
  ExactlyOne xor_1 (.out(xor_1_out), .in0(decoder_1_out0[0]), .in1(decoder_1_out0[1]), .in2(decoder_1_out0[2]));
  Multiplexer #(.select(3), .width(8)) multiplexer_4 (
    .in0({8{1'b0}}), .in1(WD_data), .in2(WD_arith1), .in3({8{1'b0}}), .in4(WD_arith2), .in5({8{1'b0}}),
    .in6({8{1'b0}}), .in7({8{1'b0}}), .out(multiplexer_4_out), .sel(decoder_1_out1));
  ExactlyOne xor_2 (.out(xor_2_out), .in0(decoder_1_out1[0]), .in1(decoder_1_out1[1]), .in2(decoder_1_out1[2]));
  Multiplexer #(.select(3), .width(8)) multiplexer_5 (
    .in0({8{1'b0}}), .in1(WD_data), .in2(WD_arith1), .in3({8{1'b0}}), .in4(WD_arith2), .in5({8{1'b0}}),
    .in6({8{1'b0}}), .in7({8{1'b0}}), .out(multiplexer_5_out), .sel(decoder_1_out2));
  ExactlyOne xor_3 (.out(xor_3_out), .in0(decoder_1_out2[0]), .in1(decoder_1_out2[1]), .in2(decoder_1_out2[2]));
  Multiplexer #(.select(3), .width(8)) multiplexer_6 (
    .in0({8{1'b0}}), .in1(WD_data), .in2(WD_arith1), .in3({8{1'b0}}), .in4(WD_arith2), .in5({8{1'b0}}),
    .in6({8{1'b0}}), .in7({8{1'b0}}), .out(multiplexer_6_out), .sel(decoder_1_out3));
  ExactlyOne xor_4 (.out(xor_4_out), .in0(decoder_1_out3[0]), .in1(decoder_1_out3[1]), .in2(decoder_1_out3[2]));
  Register register_1 (.D(multiplexer_3_out), .en(xor_1_out), .clk(clk), .Q(reg_00), .clr(1'b0));
  Register register_2 (.D(multiplexer_4_out), .en(xor_2_out), .clk(clk), .Q(reg_01), .clr(1'b0));
  Register register_3 (.D(multiplexer_5_out), .en(xor_3_out), .clk(clk), .Q(reg_02), .clr(1'b0));
  Register register_4 (.D(multiplexer_6_out), .en(xor_4_out), .clk(clk), .Q(reg_03), .clr(1'b0));
  // Probe on reg_00
  // Probe on reg_01
  // Probe on reg_02
  // Probe on reg_03
  Multiplexer #(.select(2), .width(8)) multiplexer_7 (
    .in0(reg_00), .in1(reg_01), .in2(reg_02), .in3(reg_03), .out(data_output[15:8]), .sel(data_a_address));
  Multiplexer #(.select(2), .width(8)) multiplexer_8 (
    .in0(reg_00), .in1(reg_01), .in2(reg_02), .in3(reg_03), .out(multiplexer_8_out), .sel(data[1:0]));
  Multiplexer #(.select(2), .width(8)) multiplexer_9 (
    .in0(reg_00), .in1(reg_01), .in2(reg_02), .in3(reg_03), .out(arithm1_output[15:8]), .sel(arithm1[3:2]));
  Multiplexer #(.select(2), .width(8)) multiplexer_10 (
    .in0(reg_00), .in1(reg_01), .in2(reg_02), .in3(reg_03), .out(arithm1_output[7:0]), .sel(arithm1[1:0]));
  Multiplexer #(.select(2), .width(8)) multiplexer_11 (
    .in0(reg_00), .in1(reg_01), .in2(reg_02), .in3(reg_03), .out(arithm2_output[15:8]), .sel(arithm2[3:2]));
  Multiplexer #(.select(2), .width(8)) multiplexer_12 (
    .in0(reg_00), .in1(reg_01), .in2(reg_02), .in3(reg_03), .out(arithm2_output[7:0]), .sel(arithm2[1:0]));
  Multiplexer #(.select(2), .width(8)) multiplexer_13 (
    .in0(reg_00), .in1(reg_01), .in2(reg_02), .in3(reg_03), .out(ctrl_output[15:8]), .sel(ctrl_a_address));
  Multiplexer #(.select(2), .width(8)) multiplexer_14 (
    .in0(reg_00), .in1(reg_01), .in2(reg_02), .in3(reg_03), .out(multiplexer_14_out), .sel(ctrl[1:0]));
  Multiplexer #(.width(8)) multiplexer_15 (
    .in0(multiplexer_8_out), .in1(data_immediate), .out(data_output[7:0]), .sel(data[5]));
  Multiplexer #(.width(8)) multiplexer_16 (
    .in0(multiplexer_14_out), .in1(ctrl_immediate), .out(ctrl_output[7:0]), .sel(ctrl[5]));

  // Other names for the same wires on the sheet: ctrl_b_address[1:0] = ctrl[1:0]; data_b_address[1:0] = data[1:0];
  //   arithm1_b_address[1:0] = arithm1[1:0]; arithm1_a_address[1:0] = arithm1[3:2]; arithm1_WE = arithm1[4];
  //   arithm2_b_address[1:0] = arithm2[1:0]; arithm2_a_address[1:0] = arithm2[3:2]; arithm2_WE = arithm2[4];
  //   ctrl_WE = ctrl[4]; ctrl_I_type = ctrl[5]; data_WE = data[4]; data_I_type = data[5]
endmodule

module Control_unit (
  input  [7:0] i_00,
  input  [7:0] i_01,
  input  [7:0] i_02,
  input  [7:0] i_03,
  output [5:0] data,
  output [5:0] arithm1,
  output [5:0] arithm2,
  output [5:0] ctrl,
  output [2:0] data_FU_selector,
  output [2:0] arith1_FU_selector,
  output [2:0] arith2_FU_selector,
  output [2:0] ctrl_FU_selector,
  output mem_to_reg,
  output mem_write,
  output [1:0] PC_handler
);

  wire decoder_1_out0, decoder_1_out1, decoder_1_out2, decoder_1_out3, decoder_2_out0, decoder_2_out1,
       decoder_2_out2, decoder_2_out3, decoder_3_out0, decoder_3_out1, decoder_3_out2, decoder_3_out3,
       decoder_4_out0, decoder_4_out1, decoder_4_out2, decoder_4_out3, first_mem_to_reg, first_mem_Write,
       fourth_mem_to_reg, fourth_mem_Write, not_1_out, not_2_out, not_3_out, not_4_out, second_mem_to_reg,
       second_mem_Write, third_mem_to_reg, third_mem_Write;
  wire [1:0] first_PC_handler, fourth_PC_handler, second_PC_handler, third_PC_handler;
  wire [2:0] arithm1_instruction_selector, arithm2_instruction_selector, ctrl_instruction_selector,
       data_instruction_selector, first_FU_op_selector, fourth_FU_op_selector,
       Instruction0_control_memory_data, Instruction1_control_memory_data, Instruction2_control_memory_data,
       Instruction3_control_memory_data, second_FU_op_selector, third_FU_op_selector;
  wire [5:4] first_instruction, fourth_instruction, second_instruction, third_instruction;

  ROM #(.addrWidth(4), .dataWidth(12)) Instruction0_control_memory (
    .addr(i_00[7:4]),
    .data({first_PC_handler, first_mem_to_reg, first_mem_Write, first_instruction, first_FU_op_selector, Instruction0_control_memory_data}));
  ROM #(.addrWidth(4), .dataWidth(12)) Instruction1_control_memory (
    .addr(i_01[7:4]),
    .data({second_PC_handler, second_mem_to_reg, second_mem_Write, second_instruction, second_FU_op_selector, Instruction1_control_memory_data}));
  ROM #(.addrWidth(4), .dataWidth(12)) Instruction2_control_memory (
    .addr(i_02[7:4]),
    .data({third_PC_handler, third_mem_to_reg, third_mem_Write, third_instruction, third_FU_op_selector, Instruction2_control_memory_data}));
  ROM #(.addrWidth(4), .dataWidth(12)) Instruction3_control_memory (
    .addr(i_03[7:4]),
    .data({fourth_PC_handler, fourth_mem_to_reg, fourth_mem_Write, fourth_instruction, fourth_FU_op_selector, Instruction3_control_memory_data}));
  not not_1 (not_1_out, Instruction0_control_memory_data[2]);
  not not_2 (not_2_out, Instruction1_control_memory_data[2]);
  not not_3 (not_3_out, Instruction2_control_memory_data[2]);
  not not_4 (not_4_out, Instruction3_control_memory_data[2]);
  Decoder #(.select(2)) decoder_1 (
    .out0(decoder_1_out0), .out1(decoder_1_out1), .out2(decoder_1_out2), .out3(decoder_1_out3),
    .sel(Instruction0_control_memory_data[1:0]), .en(not_1_out));
  Decoder #(.select(2)) decoder_2 (
    .out0(decoder_2_out0), .out1(decoder_2_out1), .out2(decoder_2_out2), .out3(decoder_2_out3),
    .sel(Instruction1_control_memory_data[1:0]), .en(not_2_out));
  Decoder #(.select(2)) decoder_3 (
    .out0(decoder_3_out0), .out1(decoder_3_out1), .out2(decoder_3_out2), .out3(decoder_3_out3),
    .sel(Instruction2_control_memory_data[1:0]), .en(not_3_out));
  Decoder #(.select(2)) decoder_4 (
    .out0(decoder_4_out0), .out1(decoder_4_out1), .out2(decoder_4_out2), .out3(decoder_4_out3),
    .sel(Instruction3_control_memory_data[1:0]), .en(not_4_out));
  // NoConnect on decoder_1_out3
  // NoConnect on decoder_2_out3
  // NoConnect on decoder_3_out3
  // NoConnect on decoder_4_out3
  Selector_3bits u_data_instruction_selector (
    .i_00(decoder_1_out0), .i_01(decoder_2_out0), .i_02(decoder_3_out0), .i_03(decoder_4_out0),
    .selected(data_instruction_selector));
  Selector_arithm_3bits arithm_instruction_selector (
    .instruction_00(decoder_1_out1), .instruction_01(decoder_2_out1), .instruction_02(decoder_3_out1),
    .instruction_03(decoder_4_out1), .arithm1(arithm1_instruction_selector),
    .arithm2(arithm2_instruction_selector));
  Selector_3bits u_ctrl_instruction_selector (
    .i_00(decoder_1_out2), .i_01(decoder_2_out2), .i_02(decoder_3_out2), .i_03(decoder_4_out2),
    .selected(ctrl_instruction_selector));
  Multiplexer #(.select(3), .width(6)) multiplexer_1 (
    .in0({first_instruction, i_00[3:0]}), .in1({second_instruction, i_01[3:0]}),
    .in2({third_instruction, i_02[3:0]}), .in3({fourth_instruction, i_03[3:0]}), .in4({6{1'b0}}),
    .in5({6{1'b0}}), .in6({6{1'b0}}), .in7({6{1'b0}}), .out(data), .sel(data_instruction_selector));
  Multiplexer #(.select(3), .width(6)) multiplexer_2 (
    .in0({first_instruction, i_00[3:0]}), .in1({second_instruction, i_01[3:0]}),
    .in2({third_instruction, i_02[3:0]}), .in3({fourth_instruction, i_03[3:0]}), .in4({6{1'b0}}),
    .in5({6{1'b0}}), .in6({6{1'b0}}), .in7({6{1'b0}}), .out(arithm1), .sel(arithm1_instruction_selector));
  Multiplexer #(.select(3), .width(6)) multiplexer_3 (
    .in0({first_instruction, i_00[3:0]}), .in1({second_instruction, i_01[3:0]}),
    .in2({third_instruction, i_02[3:0]}), .in3({fourth_instruction, i_03[3:0]}), .in4({6{1'b0}}),
    .in5({6{1'b0}}), .in6({6{1'b0}}), .in7({6{1'b0}}), .out(arithm2), .sel(arithm2_instruction_selector));
  Multiplexer #(.select(3), .width(6)) multiplexer_4 (
    .in0({first_instruction, i_00[3:0]}), .in1({second_instruction, i_01[3:0]}),
    .in2({third_instruction, i_02[3:0]}), .in3({fourth_instruction, i_03[3:0]}), .in4({6{1'b0}}),
    .in5({6{1'b0}}), .in6({6{1'b0}}), .in7({6{1'b0}}), .out(ctrl), .sel(ctrl_instruction_selector));
  Multiplexer #(.select(3), .width(3)) multiplexer_5 (
    .in0(first_FU_op_selector), .in1(second_FU_op_selector), .in2(third_FU_op_selector),
    .in3(fourth_FU_op_selector), .in4(3'b111), .in5(3'b111), .in6(3'b111), .in7(3'b111),
    .out(data_FU_selector), .sel(data_instruction_selector));
  Multiplexer #(.select(3), .width(3)) multiplexer_6 (
    .in0(first_FU_op_selector), .in1(second_FU_op_selector), .in2(third_FU_op_selector),
    .in3(fourth_FU_op_selector), .in4(3'b111), .in5(3'b111), .in6(3'b111), .in7(3'b111),
    .out(arith1_FU_selector), .sel(arithm1_instruction_selector));
  Multiplexer #(.select(3), .width(3)) multiplexer_7 (
    .in0(first_FU_op_selector), .in1(second_FU_op_selector), .in2(third_FU_op_selector),
    .in3(fourth_FU_op_selector), .in4(3'b111), .in5(3'b111), .in6(3'b111), .in7(3'b111),
    .out(arith2_FU_selector), .sel(arithm2_instruction_selector));
  Multiplexer #(.select(3), .width(3)) multiplexer_8 (
    .in0(first_FU_op_selector), .in1(second_FU_op_selector), .in2(third_FU_op_selector),
    .in3(fourth_FU_op_selector), .in4(3'b111), .in5(3'b111), .in6(3'b111), .in7(3'b111),
    .out(ctrl_FU_selector), .sel(ctrl_instruction_selector));
  or or_1 (mem_to_reg, first_mem_to_reg, second_mem_to_reg, third_mem_to_reg, fourth_mem_to_reg);
  or or_2 (mem_write, first_mem_Write, second_mem_Write, third_mem_Write, fourth_mem_Write);
  assign PC_handler = first_PC_handler | second_PC_handler | third_PC_handler | fourth_PC_handler;  // OR_Gate or_3, 2 bits wide

  // Other names for the same wires on the sheet: first_register_handler[1:0] = first_instruction;
  //   second_register_handler[1:0] = second_instruction; third_register_handler[1:0] = third_instruction;
  //   fourth_register_handler[1:0] = fourth_instruction; fourth_instruction[3:0] = i_03[3:0];
  //   first_instruction[3:0] = i_00[3:0]; second_instruction[3:0] = i_01[3:0]; third_instruction[3:0] = i_02[3:0]

  // Notes on the sheet:
  //   contents of Instruction0_control_memory (hex, n*v repeats v):
  //   412 49a 802 88a 250 110 c0 c8 41 49 51 59 61 69 71 4
  //   contents of Instruction1_control_memory (hex, n*v repeats v):
  //   412 49a 802 88a 250 110 c0 c8 41 49 51 59 61 69 71 4
  //   contents of Instruction2_control_memory (hex, n*v repeats v):
  //   412 49a 802 88a 250 110 c0 c8 41 49 51 59 61 69 71 4
  //   contents of Instruction3_control_memory (hex, n*v repeats v):
  //   412 49a 802 88a 250 110 c0 c8 41 49 51 59 61 69 71 4
endmodule

module Selector_3bits (
  input  i_00,
  input  i_01,
  input  i_02,
  input  i_03,
  output [2:0] selected
);

  wire not_1_out, not_2_out, not_3_out, not_4_out;

  not not_1 (not_1_out, i_00);
  not not_2 (not_2_out, i_01);
  not not_3 (not_3_out, i_02);
  not not_4 (not_4_out, i_03);
  and and_1 (selected[2], not_1_out, not_2_out, not_3_out, not_4_out);
  or or_1 (selected[1], i_03, i_02);
  or or_2 (selected[0], i_03, i_01);
endmodule

module Selector_arithm_3bits (
  input  instruction_00,
  input  instruction_01,
  input  instruction_02,
  input  instruction_03,
  output [2:0] arithm1,
  output [2:0] arithm2
);

  wire and_2_out, and_3_out, and_4_out, and_5_out, and_6_out, and_7_out, and_8_out, and_9_out, and_10_out,
       and_11_out, and_12_out, and_13_out, and_14_out, and_15_out, and_16_out, and_17_out, and_18_out,
       not_1_out, not_2_out, not_3_out, not_4_out;

  not not_1 (not_1_out, instruction_00);
  not not_2 (not_2_out, instruction_01);
  not not_3 (not_3_out, instruction_02);
  not not_4 (not_4_out, instruction_03);
  and and_1 (arithm1[2], not_1_out, not_2_out, not_3_out, not_4_out);
  and and_2 (and_2_out, not_1_out, not_2_out, instruction_03);
  and and_3 (and_3_out, not_1_out, not_2_out, instruction_02);
  and and_4 (and_4_out, not_1_out, not_3_out, instruction_03);
  and and_5 (and_5_out, not_1_out, instruction_01);
  and and_6 (and_6_out, not_1_out, not_2_out, not_3_out);
  and and_7 (and_7_out, not_1_out, not_2_out, not_4_out);
  and and_8 (and_8_out, not_1_out, not_3_out, not_4_out);
  and and_9 (and_9_out, not_2_out, not_3_out, not_4_out);
  and and_10 (and_10_out, instruction_02, instruction_03);
  and and_11 (and_11_out, instruction_01, instruction_03);
  and and_12 (and_12_out, instruction_01, instruction_02);
  and and_13 (and_13_out, instruction_00, instruction_03);
  and and_14 (and_14_out, instruction_00, instruction_02);
  and and_15 (and_15_out, instruction_02, instruction_03);
  and and_16 (and_16_out, instruction_01, instruction_03);
  and and_17 (and_17_out, instruction_00, instruction_03);
  and and_18 (and_18_out, instruction_00, instruction_01);
  or or_1 (arithm1[1], and_2_out, and_3_out);
  or or_2 (arithm1[0], and_4_out, and_5_out);
  or or_3 (arithm2[2], and_6_out, and_7_out, and_8_out, and_9_out);
  or or_4 (arithm2[1], and_10_out, and_11_out, and_12_out, and_13_out, and_14_out);
  or or_5 (arithm2[0], and_15_out, and_16_out, and_17_out, and_18_out);
endmodule
